# Fritzing sketch 5958bit (saved by Fritzing 0.9.3b)
breadboards: 1

parts:
  Part1 = Arduino Uno (Rev3)
  R1 = Resistor [tolerance=±5% resistance=1k package="1206 [SMD]"]
  LCD1 = LCD screen
  U1 = 74HC595 [package="DIP16 [THT]"]

nets:
  N1: Part1.D2, LCD1.RS
  N2: Part1.D3_PWM, LCD1.E
  N3: Part1.D4, U1.DS
  N4: Part1.D5_PWM, U1.ST_CP
  N5: Part1.D6_PWM, U1.SH_CP
  5V: Part1.5V, LCD1.VDD, LCD1.LED+, U1.MR, U1.VCC
  GND: Part1.GND, R1.Pin_0, LCD1.VSS, LCD1.R/W, LCD1.LED-, U1.GND, U1.OE
  N6: R1.Pin_1, LCD1.V0
  N7: LCD1.DB0, U1.Q0
  N8: LCD1.DB1, U1.Q1
  N9: LCD1.DB2, U1.Q2
  N10: LCD1.DB3, U1.Q3
  N11: LCD1.DB4, U1.Q4
  N12: LCD1.DB5, U1.Q5
  N13: LCD1.DB6, U1.Q6
  N14: LCD1.DB7, U1.Q7
